// Logisim project and.circ as structural Verilog: 1 circuit, main circuit main
module main (
  input  Using_NAND,
  input  in_2,
  input  in_3,
  input  in_4
);

  wire nand_1_out, nand_2_out, nor_1_out, nor_2_out, nor_3_out;

  nor nor_1 (nor_1_out, in_3, in_3);
  nor nor_2 (nor_2_out, in_4, in_4);
  nand nand_1 (nand_1_out, Using_NAND, in_2, in_2);
  nor nor_3 (nor_3_out, nor_1_out, nor_2_out);
  nand nand_2 (nand_2_out, nand_1_out, nand_1_out, nand_1_out, nand_1_out);
  LED Z (.in(nor_3_out));
  LED Y (.in(nand_2_out));

  // Notes on the sheet:
  //   AND GATE:
  //   Using NOR
endmodule
