// Logisim project nand.circ as structural Verilog: 1 circuit, main circuit main
module main (
  input  in_1,
  input  in_2,
  input  in_3,
  input  in_4
);

  wire nand_1_out, nor_1_out, nor_2_out, nor_3_out, nor_4_out;

  nor nor_1 (nor_1_out, in_3, in_3);
  nor nor_2 (nor_2_out, in_4, in_4);
  nand nand_1 (nand_1_out, in_1, in_2);
  nor nor_3 (nor_3_out, nor_1_out, nor_2_out);
  LED led_1 (.in(nand_1_out));
  nor nor_4 (nor_4_out, nor_3_out, nor_3_out);
  LED led_2 (.in(nor_4_out));

  // Notes on the sheet:
  //   NAND GATE:
  //   Using NAND
  //   Using NOR
endmodule
