// Logisim project nor.circ as structural Verilog: 1 circuit, main circuit main
module main (
  input  in_1,
  input  in_2,
  input  in_3,
  input  in_4
);

  wire nand_1_out, nand_2_out, nand_3_out, nand_4_out, nor_1_out;

  nand nand_1 (nand_1_out, in_1, in_1);
  nand nand_2 (nand_2_out, in_2, in_2);
  nor nor_1 (nor_1_out, in_3, in_4);
  nand nand_3 (nand_3_out, nand_1_out, nand_2_out);
  LED led_1 (.in(nor_1_out));
  LED led_2 (.in(nand_4_out));
  nand nand_4 (nand_4_out, nand_3_out, nand_3_out);

  // Notes on the sheet:
  //   NOR GATE:
  //   Using NAND
  //   Using NOR
endmodule
