// Logisim project 10's & 9's Complement.circ as structural Verilog: 2 circuits, main circuit 10's Complement
module _10_s_Complement (
  input  A3,
  input  A2,
  input  A1,
  input  A0,
  output B3,
  output B2,
  output B1,
  output B0
);

  wire nand_1_out, nand_2_out, nand_3_out, nand_4_out, nand_5_out, nand_6_out, nand_7_out, nand_8_out,
       nand_9_out, nand_10_out, nand_11_out, nand_12_out, nand_13_out, nand_14_out, nand_15_out, nand_16_out,
       nand_17_out, nand_18_out, nand_19_out, nand_20_out;

  nand nand_1 (nand_1_out, A3, A3);
  nand nand_2 (nand_2_out, A2, A2);
  nand nand_3 (nand_3_out, A1, A1);
  nand nand_4 (nand_4_out, A3, A3);
  nand nand_5 (nand_5_out, A2, A2);
  nand nand_6 (nand_6_out, A0, A0);
  nand nand_7 (nand_7_out, A2, A2);
  nand nand_8 (nand_8_out, A1, A1);
  nand nand_9 (nand_9_out, A0, A0);
  nand nand_10 (nand_10_out, A1, A1);
  nand nand_11 (nand_11_out, A0, A0);
  nand nand_12 (nand_12_out, A3, A3);
  nand nand_13 (nand_13_out, nand_1_out, nand_2_out, nand_3_out);
  nand nand_14 (nand_14_out, nand_4_out, nand_5_out, nand_6_out);
  nand nand_15 (nand_15_out, nand_7_out, A1, A0);
  nand nand_16 (nand_16_out, A2, nand_8_out);
  nand nand_17 (nand_17_out, A2, nand_9_out);
  nand nand_18 (nand_18_out, nand_10_out, nand_11_out);
  nand nand_19 (nand_19_out, A1, A0);
  nand nand_20 (nand_20_out, nand_12_out, A0);
  nand nand_21 (B3, nand_13_out, nand_14_out);
  nand nand_22 (B2, nand_15_out, nand_16_out, nand_17_out);
  nand nand_23 (B1, nand_18_out, nand_19_out);
  nand nand_24 (B0, nand_20_out, nand_20_out);

  // Notes on the sheet:
  //   10's complement of
  //   Input Number:A3A2A1A0
  //   Output Number:B3B2B1B0
endmodule

module _9_s_Complement (
  input  A3,
  input  A2,
  input  A1,
  input  A0,
  output B3,
  output B2,
  output B1,
  output B0
);

  wire nand_1_out, nand_2_out, nand_3_out, nand_4_out, nand_5_out, nand_7_out, nand_8_out, nand_9_out;

  nand nand_1 (nand_1_out, A3, A3);
  nand nand_2 (nand_2_out, A2, A2);
  nand nand_3 (nand_3_out, A1, A1);
  nand nand_4 (nand_4_out, A2, A2);
  nand nand_5 (nand_5_out, A1, A1);
  nand nand_6 (B0, A0, A0);
  nand nand_7 (nand_7_out, nand_1_out, nand_2_out, nand_3_out);
  nand nand_8 (nand_8_out, nand_4_out, A1);
  nand nand_9 (nand_9_out, A2, nand_5_out);
  nand nand_10 (B3, nand_7_out, nand_7_out);
  nand nand_11 (B2, nand_8_out, nand_9_out);

  assign B1 = A1;

  // Notes on the sheet:
  //   Input Number:A3A2A1A0
  //   Output Number:B3B2B1B0
endmodule
