// Logisim project 9's Complement of BCD equivalent.circ as structural Verilog: 1 circuit, main circuit main
module main (
  input  A,
  input  B,
  input  C,
  input  D,
  output W,
  output X,
  output Y,
  output Z
);

  wire and_1_out, not_1_out, not_2_out, not_3_out;

  not not_1 (not_1_out, C);
  and and_1 (and_1_out, not_1_out, not_2_out);
  not not_2 (not_2_out, A);
  not not_3 (not_3_out, B);
  xor xor_1 (X, B, C);
  not not_4 (Z, D);
  and and_2 (W, and_1_out, not_3_out);

  assign Y = C;
endmodule
