// Logisim project gray_to_binary.circ as structural Verilog: 1 circuit, main circuit main
module main (
  input  A,
  input  B,
  input  C,
  input  D,
  output W,
  output X,
  output Y,
  output Z
);

  wire xor_2_out, xor_3_out, xor_4_out;

  xor xor_1 (X, A, B);
  xor xor_2 (xor_2_out, A, B);
  xor xor_3 (xor_3_out, A, B);
  xor xor_4 (xor_4_out, C, D);
  xor xor_5 (Y, xor_2_out, C);
  xor xor_6 (Z, xor_3_out, xor_4_out);

  assign W = A;
endmodule
