// Logisim project square.circ as structural Verilog: 1 circuit, main circuit main
module main (
  input  A,
  input  B,
  input  C,
  input  D,
  output W1,
  output W2,
  output W3,
  output W4,
  output W5,
  output W6,
  output W7,
  output W8
);

  wire and_2_out, and_3_out, and_6_out, and_7_out, and_8_out, and_9_out, not_1_out, not_2_out, not_3_out,
       not_4_out, or_1_out, xor_1_out, xor_2_out, xor_3_out;

  and and_1 (W1, A, B);
  not not_1 (not_1_out, B);
  or or_1 (or_1_out, not_1_out, C);
  xor xor_1 (xor_1_out, A, B);
  and and_2 (and_2_out, A, B);
  xor xor_2 (xor_2_out, A, B);
  and and_3 (and_3_out, B, not_2_out);
  not not_2 (not_2_out, C);
  not not_3 (not_3_out, D);
  xor xor_3 (xor_3_out, B, C);
  and and_4 (W6, C, not_4_out);
  not not_4 (not_4_out, D);
  and and_5 (W2, A, or_1_out);
  and and_6 (and_6_out, xor_1_out, C);
  and and_7 (and_7_out, and_2_out, D);
  and and_8 (and_8_out, xor_2_out, D);
  and and_9 (and_9_out, and_3_out, not_3_out);
  and and_10 (W5, xor_3_out, D);
  or or_2 (W3, and_6_out, and_7_out);
  or or_3 (W4, and_8_out, and_9_out);

  assign W7 = 1'b0;
  assign W8 = D;
endmodule
