// Logisim project 4 bit binary adder and subtractor using MUX.circ as structural Verilog: 1 circuit, main circuit main
module main (
  input  in_1,
  input  B0,
  input  A0,
  input  B1,
  input  A1,
  input  B2,
  input  A2,
  input  B3,
  input  A3
);

  wire multiplexer_1_out, multiplexer_2_out, multiplexer_3_out, multiplexer_4_out, multiplexer_5_out,
       multiplexer_6_out, multiplexer_7_out, multiplexer_8_out, not_1_out, not_2_out, not_3_out, not_4_out,
       xor_1_out, xor_2_out, xor_3_out, xor_4_out, xor_5_out, xor_6_out, xor_7_out, xor_8_out;

  xor xor_1 (xor_1_out, in_1, B0);
  xor xor_2 (xor_2_out, in_1, B1);
  xor xor_3 (xor_3_out, in_1, B2);
  xor xor_4 (xor_4_out, in_1, B3);
  not not_1 (not_1_out, in_1);
  not not_2 (not_2_out, multiplexer_2_out);
  not not_3 (not_3_out, multiplexer_4_out);
  xor xor_5 (xor_5_out, xor_1_out, A0);
  xor xor_6 (xor_6_out, xor_2_out, A1);
  xor xor_7 (xor_7_out, xor_3_out, A2);
  not not_4 (not_4_out, multiplexer_6_out);
  xor xor_8 (xor_8_out, xor_4_out, A3);
  Multiplexer multiplexer_1 (.in0(in_1), .in1(not_1_out), .out(multiplexer_1_out), .sel(xor_5_out));  // open: en
  Multiplexer multiplexer_2 (.in0(A0), .in1(in_1), .out(multiplexer_2_out), .sel(xor_5_out));  // open: en
  Multiplexer multiplexer_3 (
    .in0(multiplexer_2_out), .in1(not_2_out), .out(multiplexer_3_out), .sel(xor_6_out));  // open: en
  Multiplexer multiplexer_4 (.in0(A1), .in1(multiplexer_2_out), .out(multiplexer_4_out), .sel(xor_6_out));  // open: en
  Multiplexer multiplexer_5 (
    .in0(multiplexer_4_out), .in1(not_3_out), .out(multiplexer_5_out), .sel(xor_7_out));  // open: en
  Multiplexer multiplexer_6 (.in0(A2), .in1(multiplexer_4_out), .out(multiplexer_6_out), .sel(xor_7_out));  // open: en
  Multiplexer multiplexer_7 (
    .in0(multiplexer_6_out), .in1(not_4_out), .out(multiplexer_7_out), .sel(xor_8_out));  // open: en
  Multiplexer multiplexer_8 (.in0(A3), .in1(multiplexer_6_out), .out(multiplexer_8_out), .sel(xor_8_out));  // open: en
  LED led_1 (.in(multiplexer_1_out));
  LED led_2 (.in(multiplexer_3_out));
  LED led_3 (.in(multiplexer_5_out));
  LED led_4 (.in(multiplexer_7_out));
  LED led_5 (.in(multiplexer_8_out));

  // Notes on the sheet:
  //   S0
  //   S1
  //   s2
  //   s3
  //   s4
endmodule
