// Logisim project not.circ as structural Verilog: 1 circuit, main circuit main
module main (
  input  in_1,
  input  in_2
);

  wire nand_1_out, nor_1_out;

  nand nand_1 (nand_1_out, in_1, in_1);
  nor nor_1 (nor_1_out, in_2, in_2);
  LED led_1 (.in(nand_1_out));
  LED led_2 (.in(nor_1_out));

  // Notes on the sheet:
  //   NOT GATE:
  //   Using NAND
  //   Using NOR
endmodule
