// Logisim project or.circ as structural Verilog: 1 circuit, main circuit main
module main (
  input  in_1,
  input  in_2,
  input  Using_NOR,
  input  in_4
);

  wire nand_1_out, nand_2_out, nand_3_out, nor_1_out, nor_2_out;

  nand nand_1 (nand_1_out, in_1, in_1);
  nand nand_2 (nand_2_out, in_2, in_2);
  nor nor_1 (nor_1_out, Using_NOR, in_4);
  nand nand_3 (nand_3_out, nand_1_out, nand_2_out);
  nor nor_2 (nor_2_out, nor_1_out, nor_1_out);
  LED led_1 (.in(nand_3_out));
  LED led_2 (.in(nor_2_out));

  // Notes on the sheet:
  //   OR GATE:
  //   Using NAND
endmodule
