// Logisim project bcd_to_excess3.circ as structural Verilog: 1 circuit, main circuit main
module main (
  input  A,
  input  B,
  input  C,
  input  D,
  output W,
  output X,
  output Y,
  output Z
);

  wire and_1_out, or_1_out, or_2_out;

  or or_1 (or_1_out, C, D);
  or or_2 (or_2_out, C, D);
  xnor xnor_1 (Y, C, D);
  not not_1 (Z, D);
  or or_3 (W, A, and_1_out);
  and and_1 (and_1_out, B, or_1_out);
  xor xor_1 (X, B, or_2_out);
endmodule
