// Logisim project excess3_to_bcd.circ as structural Verilog: 1 circuit, main circuit main
module main (
  input  A,
  input  B,
  input  C,
  input  D,
  output W,
  output X,
  output Y,
  output Z
);

  wire and_1_out, nand_1_out, or_1_out;

  and and_1 (and_1_out, C, D);
  nand nand_1 (nand_1_out, C, D);
  xor xor_1 (Y, C, D);
  not not_1 (Z, D);
  and and_2 (W, A, or_1_out);
  or or_1 (or_1_out, B, and_1_out);
  xor xor_2 (X, B, nand_1_out);
endmodule
