// Logisim project HalfSubtractor.circ as structural Verilog: 1 circuit, main circuit main
module main (
  input  A,
  input  B,
  output DIFFERENCE,
  output BORROW
);

  wire not_1_out;

  xor xor_1 (DIFFERENCE, A, B);
  not not_1 (not_1_out, A);
  and and_1 (BORROW, not_1_out, B);

  // Notes on the sheet:
  //   HALF SUBTRACTOR
endmodule
