// Logisim project 4 bit binary adder and subtractor using DECODER.circ as structural Verilog: 1 circuit, main circuit main
module main (
  input  in_1,
  input  B0,
  input  A0,
  input  B1,
  input  A1,
  input  B2,
  input  A2,
  input  B3,
  input  A3
);

  wire decoder_1_out0, decoder_1_out1, decoder_1_out2, decoder_1_out3, decoder_1_out4, decoder_1_out5,
       decoder_1_out6, decoder_1_out7, decoder_2_out0, decoder_2_out1, decoder_2_out2, decoder_2_out3,
       decoder_2_out4, decoder_2_out5, decoder_2_out6, decoder_2_out7, decoder_3_out0, decoder_3_out1,
       decoder_3_out2, decoder_3_out3, decoder_3_out4, decoder_3_out5, decoder_3_out6, decoder_3_out7,
       decoder_4_out0, decoder_4_out1, decoder_4_out2, decoder_4_out3, decoder_4_out4, decoder_4_out5,
       decoder_4_out6, decoder_4_out7, or_1_out, or_2_out, or_3_out, or_5_out, or_6_out;
  wire [1:0] or_4_out, or_7_out, or_8_out;
  wire [1:1] xor_1_out;

  xor xor_1 (xor_1_out[1], in_1, B0);
  xor xor_2 (or_7_out[1], in_1, B1);
  xor xor_3 (or_8_out[1], in_1, B2);
  xor xor_4 (or_4_out[1], in_1, B3);
  Decoder #(.select(3), .enable("false")) decoder_1 (
    .out0(decoder_1_out0), .out1(decoder_1_out1), .out2(decoder_1_out2), .out3(decoder_1_out3),
    .out4(decoder_1_out4), .out5(decoder_1_out5), .out6(decoder_1_out6), .out7(decoder_1_out7),
    .sel({A1, or_7_out}));
  Decoder #(.select(3), .enable("false")) decoder_2 (
    .out0(decoder_2_out0), .out1(decoder_2_out1), .out2(decoder_2_out2), .out3(decoder_2_out3),
    .out4(decoder_2_out4), .out5(decoder_2_out5), .out6(decoder_2_out6), .out7(decoder_2_out7),
    .sel({A2, or_8_out}));
  Decoder #(.select(3), .enable("false")) decoder_3 (
    .out0(decoder_3_out0), .out1(decoder_3_out1), .out2(decoder_3_out2), .out3(decoder_3_out3),
    .out4(decoder_3_out4), .out5(decoder_3_out5), .out6(decoder_3_out6), .out7(decoder_3_out7),
    .sel({A3, or_4_out}));
  Decoder #(.select(3), .enable("false")) decoder_4 (
    .out0(decoder_4_out0), .out1(decoder_4_out1), .out2(decoder_4_out2), .out3(decoder_4_out3),
    .out4(decoder_4_out4), .out5(decoder_4_out5), .out6(decoder_4_out6), .out7(decoder_4_out7),
    .sel({A0, xor_1_out[1], in_1}));
  LED led_1 (.in(or_1_out));
  or or_1 (or_1_out, decoder_4_out1, decoder_4_out2, decoder_4_out4, decoder_4_out7);
  or or_2 (or_2_out, decoder_1_out1, decoder_1_out2, decoder_1_out4, decoder_1_out7);
  LED led_2 (.in(or_2_out));
  or or_3 (or_3_out, decoder_2_out1, decoder_2_out2, decoder_2_out4, decoder_2_out7);
  LED led_3 (.in(or_3_out));
  or or_4 (or_4_out[0], decoder_2_out3, decoder_2_out5, decoder_2_out6, decoder_2_out7);
  or or_5 (or_5_out, decoder_3_out1, decoder_3_out2, decoder_3_out4, decoder_3_out7);
  LED led_4 (.in(or_5_out));
  or or_6 (or_6_out, decoder_3_out3, decoder_3_out5, decoder_3_out6, decoder_3_out7);
  or or_7 (or_7_out[0], decoder_4_out3, decoder_4_out5, decoder_4_out6, decoder_4_out7);
  or or_8 (or_8_out[0], decoder_1_out3, decoder_1_out5, decoder_1_out6, decoder_1_out7);
  LED led_5 (.in(or_6_out));

  // Notes on the sheet:
  //   m0
  //   m0
  //   m0
  //   m0
  //   m2
  //   m1
  //   m2
  //   m7
  //   m1
  //   m2
  //   m7
  //   m1
  //   m2
  //   m3
  //   m4
  //   m5
  //   m6
  //   m7
  //   m1
  //   m3
  //   m4
  //   m5
  //   m6
  //   m7
  //   m3
  //   m4
  //   m5
  //   m6
  //   m3
  //   m4
  //   m5
  //   m6
  //   SUM
  //   SUM
  //   SUM
  //   S0
  //   CARRY
  //   SUM
  //   S1
  //   CARRY
  //   S2
  //   CARRY
  //   S3
  //   CARRY
  //   S4
endmodule
